// Logisim project componentes_basicos.circ as structural Verilog: 1 circuit, main circuit main
module main (
  input  in_1,
  input  in_2,
  input  in_3,
  input  in_4,
  input  in_5,
  input  in_6,
  input  in_7,
  input  in_8,
  input  in_9,
  input  in_10,
  input  in_11,
  input  in_12,
  input  in_13,
  input  in_14,
  input  in_15,
  input  in_16,
  input  in_17,
  input  in_18,
  input  in_19,
  input  in_20,
  input  in_21,
  input  in_22,
  input  in_23,
  input  in_24,
  input  in_25,
  input  in_26,
  input  in_27
);

  wire [2:0] counter_1_q;
  wire [3:0] adder_1_out, multiplexer_1_out, register_1_q;
  wire [7:0] rom_1_data;

  LED led_1 (.in(counter_1_q[2]));
  Counter #(.width(3), .max('h7), .trigger("falling")) counter_1 (
    .Q(counter_1_q), .clk(in_23));  // open: load, D, count, carry, clr
  LED led_2 (.in(rom_1_data[7]));
  Adder #(.width(4)) adder_1 (
    .a({in_10, in_11, in_12, in_13}), .b({in_14, in_15, in_16, in_17}), .out(adder_1_out), .cin(1'b0));  // open: cout
  LED led_3 (.in(counter_1_q[0]));
  LED led_4 (.in(counter_1_q[1]));
  LED led_5 (.in(rom_1_data[6]));
  LED led_6 (.in(rom_1_data[5]));
  LED led_7 (.in(rom_1_data[4]));
  Multiplexer #(.width(4)) multiplexer_1 (
    .in0({in_4, in_3, in_2, in_1}), .in1({in_8, in_7, in_6, in_5}), .out(multiplexer_1_out), .sel(in_9));  // open: en
  LED led_8 (.in(adder_1_out[3]));
  LED led_9 (.in(adder_1_out[2]));
  LED led_10 (.in(register_1_q[3]));
  Register #(.width(4)) register_1 (.D({in_18, in_19, in_20, in_21}), .Q(register_1_q), .clk(in_22));  // open: en, clr
  LED led_11 (.in(rom_1_data[3]));
  LED led_12 (.in(multiplexer_1_out[3]));
  LED led_13 (.in(multiplexer_1_out[2]));
  LED led_14 (.in(adder_1_out[0]));
  LED led_15 (.in(adder_1_out[1]));
  LED led_16 (.in(register_1_q[0]));
  LED led_17 (.in(register_1_q[1]));
  LED led_18 (.in(register_1_q[2]));
  LED led_19 (.in(rom_1_data[0]));
  LED led_20 (.in(rom_1_data[2]));
  LED led_21 (.in(rom_1_data[1]));
  ROM #(.addrWidth(4)) rom_1 (.addr({in_24, in_25, in_26, in_27}), .data(rom_1_data));  // open: sel
  LED led_22 (.in(multiplexer_1_out[1]));
  LED led_23 (.in(multiplexer_1_out[0]));

  // Notes on the sheet:
  //   MULTIPLEXADOR
  //   SOMADOR
  //   REGISTRADOR
  //   CONTADOR
  //   MEMÓRIA
endmodule
