// Logisim project unidade_de_execucao_vf.circ as structural Verilog: 1 circuit, main circuit main
module main (
  input  in_1,
  input  in_2,
  input  in_3,
  input  in_4,
  input  in_5,
  input  in_6,
  input  in_7,
  input  in_8
);

  wire and_1_out, and_2_out, clock_1_out;
  wire [3:0] adder_1_out, multiplexer_1_out, multiplexer_2_out, register_1_q, register_2_q;

  Clock clock_1 (.out(clock_1_out));
  and and_1 (and_1_out, in_3, clock_1_out);
  and and_2 (and_2_out, in_4, clock_1_out);
  LED led_1 (.in(register_1_q[3]));
  LED led_2 (.in(register_1_q[1]));
  LED led_3 (.in(register_1_q[2]));
  LED led_4 (.in(register_1_q[0]));
  Register #(.width(4)) register_1 (.D(adder_1_out), .Q(register_1_q), .clk(and_1_out));  // open: en, clr
  Register #(.width(4)) register_2 (.D(adder_1_out), .Q(register_2_q), .clk(and_2_out));  // open: en, clr
  LED led_5 (.in(register_2_q[2]));
  LED led_6 (.in(register_2_q[3]));
  LED led_7 (.in(register_2_q[1]));
  LED led_8 (.in(register_2_q[0]));
  Multiplexer #(.width(4)) multiplexer_1 (
    .in0({in_5, in_6, in_7, in_8}), .in1(register_1_q), .out(multiplexer_1_out), .sel(in_2));  // open: en
  Multiplexer #(.width(4)) multiplexer_2 (
    .in0(4'b0000), .in1(register_2_q), .out(multiplexer_2_out), .sel(in_1));  // open: en
  Adder #(.width(4)) adder_1 (
    .a(multiplexer_1_out), .b(multiplexer_2_out), .out(adder_1_out), .cin(1'b0));  // open: cout
endmodule
